# Fritzing sketch Programming circuit diagram (saved by Fritzing 0.9.3b)
breadboards: 1

parts:
  Raspberry_Pi_1 = Raspberry Pi 3 [part_number=RPI-3-V1.2]
  IC1 = L293D [package=THT]
  IC2 = L293D [package=THT]
  M1 = DC Motor  # not connected
  M2 = DC Motor  # not connected
  M3 = DC Motor  # not connected
  M4 = DC Motor  # not connected
  IC3 = MCP23017 I2C I/O Expander

nets:
  N1: Raspberry_Pi_1.3v3, IC3.RESET
  N2: Raspberry_Pi_1.GPIO2, IC3.SDA
  N3: Raspberry_Pi_1.GPIO3, IC3.SCL
  N4: Raspberry_Pi_1.GIPO5, IC1.In_4
  N5: Raspberry_Pi_1.GIPO6, IC1.In_3
  N6: Raspberry_Pi_1.GIPO13, IC1.In_1
  N7: Raspberry_Pi_1.GIPO19, IC1.In_2
  N8: Raspberry_Pi_1.GIPO26, IC2.In_1
  N9: Raspberry_Pi_1.GIPO21, IC2.In_2
  N10: Raspberry_Pi_1.GIPO20, IC2.In_3
  N11: Raspberry_Pi_1.GIPO16, IC2.In_4
  N12: Raspberry_Pi_1.GIPO18, IC2.Enable_2
  GND: Raspberry_Pi_1.GND, IC1.0V, IC2.0V, IC3.VSS, IC3.A0
  N13: Raspberry_Pi_1.5V, IC2.+V

notes:
  12V DC
  1 2 3 4 5 6
  M+ M- VCC GND CH A CH B
  Since the pi only has one hardware PWM port, I have connected all of the EN (speed) ports to the same hardware PWM pin.
  This should work fine, and better yet it should result in the exact same signal for each motor.
  Should we connect the battery and pi grounds together?
  MCP23017 pins A0-A2 are grounded as they create the reference number for the chip which in this case is chip #0

custom parts:
  MCP23017 I2C I/O Expander: The MCP23017 uses two i2c pins (these can be shared with other i2c devices), and in exchange gives you 16 general purpose pins. You can set each of 16 pins to be input, output, input with a pullup or open drain. There's even the ability to get an interrupt via an external pin when any of the inputs change so you don't have to keep polling the chip.
